# Fritzing sketch Rotary encoder (saved by Fritzing 1.0.2b)
breadboards: 1

parts:
  RE1 = Rotary Encoder [package=THT]
  Part1 = Arduino Uno (Rev3) - ICSP

nets:
  N1: RE1.EncoderPinA, Part1.GND
  N2: RE1.EncoderPinC, Part1.5V
  N3: RE1.EncoderPinB, Part1.D13/SCK
