# Fritzing sketch teabagger (saved by Fritzing 1.0.3b)
breadboards: 1

parts:
  A1 = Arduino Uno (Rev3)
  Stepper_motor_controller = Pololu A4988 [package=SO16]
  M1 = Stepper Motor - Bipolar
  C1 = Electrolytic Capacitor [capacitance=0.1mF voltage=50V package="100 mil [THT, electrolytic]"]
  V5 = DC Power [voltage=12V]
  U1 = LCD-16X2 [package=lcd-16x2]
  R1 = 6mm Trimmer Potentiometer [maximum_resistance=10kΩ knob_status=50% power=0.5W package=THT]
  R2 = Resistor [tolerance=±5% power=0.25W resistance=330 package=THT]
  rotary_encoder = rotary encoder - mille
  T2 = LM35 Temperature Sensor [thermistor_type=NTC part_number=DS18B20 package="TO92 [THT]"]

nets:
  Pin 8: A1.D8, Stepper_motor_controller.STEP
  Pin 9: A1.D9_PWM, Stepper_motor_controller.DIR
  Pin 10: A1.D10_PWM/SS, T2.Vout
  Pin 11: A1.D11_PWM/MOSI, rotary_encoder.CLK
  Pin 12: A1.D12/MISO, rotary_encoder.DT
  Pin 13: A1.D13/SCK, rotary_encoder.SW
  Pin 2: A1.D2, U1.DB7
  Pin 3: A1.D3_PWM, U1.DB6
  Pin 4: A1.D4, U1.DB5
  Pin 5: A1.D5_PWM, U1.DB4
  Pin 6: A1.D6_PWM, U1.E
  Pin 7: A1.D7, U1.RS
  5V: A1.5V, Stepper_motor_controller.VDD, U1.VDD, R1.leg1, R2.Pin_0, rotary_encoder.+, T2.+Vs
  GND: A1.GND, Stepper_motor_controller.GND, C1.-, V5.V-, U1.VSS, U1.R_W, U1.K, R1.leg2, rotary_encoder.GND, T2.GND
  12V: A1.VIN, Stepper_motor_controller.VMOT, C1.+, V5.V+
  N1: Stepper_motor_controller.RESET, Stepper_motor_controller.SLEEP
  N2: Stepper_motor_controller.1B, M1.D
  N3: Stepper_motor_controller.1A, M1.B
  N4: Stepper_motor_controller.2A, M1.C
  N5: Stepper_motor_controller.2B, M1.A
  N6: U1.VO, R1.wiper
  N7: U1.A, R2.Pin_1

notes:
  Logic voltage

custom parts:
  rotary encoder - mille: Yumo E6B2-C incremental encoder. Resolutions 10 to 4000 pulses per revolution (depending on model number). Power from 5 to 24V (again depending on model). Dia 40mm body 30mm plus 20mm shaft.
